# Fritzing sketch wiring (saved by Fritzing 0.9.4)
breadboards: 1

parts:
  Part1 = Arduino Uno (Rev3)
  LED1 = LED - 5mm [color="Red (633nm)" package="5 mm [THT]"]
  R1 = Resistor [tolerance=±5% resistance=220 package=THT]
  R2 = Resistor [tolerance=±5% resistance=220 package=THT]

nets:
  N1: Part1.D8, Part1.5V, R2.Pin_1
  N2: Part1.D9_PWM, LED1.anode
  N3: Part1.GND, R1.Pin_0, R2.Pin_0
  N4: LED1.cathode, R1.Pin_1
