# Fritzing sketch wiring (saved by Fritzing 0.9.4)
breadboards: 1

parts:
  Part1 = Arduino Uno (Rev3)
  LED1 = LED - 5mm [color="Red (635nm)" package="5 mm [THT]"]
  LED2 = smd LED [color="Green (565nm)" package="1206 [SMD]"]
  R1 = Resistor [tolerance=±5% resistance=220 package=THT]
  R2 = Resistor [tolerance=±5% resistance=220 package=THT]

nets:
  N1: Part1.D9_PWM, R2.Pin_0
  N2: Part1.D10_PWM/SS, R1.Pin_0
  N3: Part1.GND, LED1.cathode, LED2.cathode
  N4: LED1.anode, R1.Pin_1
  N5: LED2.anode, R2.Pin_1
