# Fritzing sketch wiring (saved by Fritzing 0.9.4)
breadboards: 1

parts:
  Part1 = Arduino Uno (Rev3)
  hc-sr1 = hc-sr04
  LED2 = smd LED [color="Red (633nm)" package="1206 [SMD]"]
  LED3 = smd LED [color="Green (555nm)" package="1206 [SMD]"]
  R1 = Resistor [tolerance=±5% resistance=220 package="2010 [SMD]"]
  R2 = Resistor [tolerance=±5% resistance=220 package="2010 [SMD]"]

nets:
  N1: Part1.D9_PWM, LED2.anode
  N2: Part1.D10_PWM/SS, LED3.anode
  N3: Part1.D2, hc-sr1.Trig
  N4: Part1.D3_PWM, hc-sr1.Echo
  5V: Part1.5V, hc-sr1.VCC
  GND: Part1.GND, hc-sr1.GND, R1.Pin_0, R2.Pin_0
  N5: LED2.cathode, R1.Pin_1
  N6: LED3.cathode, R2.Pin_1
