# Fritzing sketch wiring (saved by Fritzing 0.9.4)
breadboards: 1

parts:
  Part1 = Arduino Uno (Rev3)
  R1 = Resistor [tolerance=±5% resistance=220 package=THT]
  LED1 = LED - 5mm [color="Green (560nm)" package="5 mm [THT]"]
  R3 = PHOTOCELL [package=photocell]
  R4 = Resistor [tolerance=±5% resistance=220 package=THT]

nets:
  N1: Part1.A0, R1.Pin_1, R3.P$1
  N2: Part1.D10_PWM/SS, LED1.anode
  N3: Part1.GND, R1.Pin_0, R3.P$2, R4.Pin_0
  N4: LED1.cathode, R4.Pin_1
